// Logisim project u16a.circ as structural Verilog: 1 circuit, main circuit main
module main (
);

  wire ADDR_WRITE, ALU_F, ALU_NO, ALU_NX, ALU_NY, ALU_OUT_NEG, ALU_OUT_ZERO, ALU_READ, ALU_ZX, ALU_ZY,
       and_1_out, and_2_out, and_3_out, and_4_out, and_5_out, and_6_out, and_7_out, and_8_out, and_9_out,
       and_10_out, and_11_out, and_12_out, and_13_out, and_14_out, and_16_out, BX_READ, BX_WRITE, BY_READ,
       BY_WRITE, BZ_READ, BZ_WRITE, CLK, demultiplexer_1_out0, demultiplexer_1_out1, demultiplexer_1_out2,
       demultiplexer_1_out3, demultiplexer_1_out4, demultiplexer_1_out5, INST_STEP_RESET, INST_WRITE,
       INV_CLK, IP_COUNT, IP_READ, IP_WRITE, not_2_out, RAM_READ, RAM_WRITE;
  wire [2:0] INST_STEP_q;
  wire [3:0] ADDR_q;
  wire [11:0] INST_q;
  wire [13:6] MICROINSTRUCTIONS_data;
  wire [14:0] multiplexer_6_out;
  wire [15:0] adder_1_out, ALU_IN_X, ALU_IN_Y, and_15_out, BZ_q, DBUS, dipswitch_1_sw16, IP_q,
       multiplexer_1_out, multiplexer_2_out, multiplexer_3_out, multiplexer_4_out, multiplexer_5_out,
       not_3_out, not_4_out, not_5_out, ram_1_dout, register_1_q, register_2_q, register_3_q, register_4_q,
       register_5_q, register_6_q;
  wire [15:4] ADDR_q_2;

  Counter #(.max('h7), .width(3)) INST_STEP (
    .clr(INST_STEP_RESET), .load(1'b0), .up(1'b1), .count(1'b1), .clk(INV_CLK), .Q(INST_STEP_q));  // open: D, carry
  Clock clock_1 (.out(CLK));
  not not_1 (INV_CLK, CLK);
  Counter #(.max('hffff), .width(16)) IP (
    .clr(1'b0), .load(IP_WRITE), .up(1'b1), .count(IP_COUNT), .clk(CLK), .D(DBUS), .Q(IP_q));  // open: carry
  Register #(.width(16)) BX (.D(DBUS), .en(BX_WRITE), .clk(CLK), .Q(ALU_IN_X));  // open: clr
  Register #(.width(16)) BY (.D(DBUS), .en(BY_WRITE), .clk(CLK), .Q(ALU_IN_Y));  // open: clr
  Register #(.width(16)) BZ (.D(DBUS), .en(BZ_WRITE), .clk(CLK), .Q(BZ_q));  // open: clr
  Register #(.width(12)) INST (.D(DBUS[11:0]), .en(INST_WRITE), .clk(CLK), .Q(INST_q));  // open: clr
  assign DBUS = BX_READ ? ALU_IN_X : 16'bz;  // Controlled_Buffer controlled_buffer_1
  assign DBUS = BY_READ ? ALU_IN_Y : 16'bz;  // Controlled_Buffer controlled_buffer_2
  assign DBUS = BZ_READ ? BZ_q : 16'bz;  // Controlled_Buffer controlled_buffer_3
  ROM #(.addrWidth(16), .dataWidth(16)) MICROINSTRUCTIONS (
    .addr({INST_q, INST_STEP_q, ALU_OUT_ZERO}),
    .data({INST_STEP_RESET, IP_COUNT, MICROINSTRUCTIONS_data, ALU_NO, ALU_F, ALU_NY, ALU_ZY, ALU_NX, ALU_ZX}));
  assign DBUS = IP_READ ? IP_q : 16'bz;  // Controlled_Buffer controlled_buffer_4
  // Probe on {INST_STEP_RESET, IP_COUNT, MICROINSTRUCTIONS_data, ALU_NO, ALU_F, ALU_NY, ALU_ZY, ALU_NX, ALU_ZX}
  Register #(.width(16)) ADDR (.D(DBUS), .en(ADDR_WRITE), .clk(CLK), .Q({ADDR_q_2, ADDR_q}));  // open: clr
  Demultiplexer #(.select(4)) demultiplexer_1 (
    .out0(demultiplexer_1_out0), .out1(demultiplexer_1_out1), .out2(demultiplexer_1_out2),
    .out3(demultiplexer_1_out3), .out4(demultiplexer_1_out4), .out5(demultiplexer_1_out5), .in(1'b1),
    .sel(ADDR_q));  // open: out6, out7, out8, out9, out10, out11, out12, out13, out14, out15
  Decoder #(.enable("false"), .select(4)) decoder_1 (
    .out1(RAM_READ), .out2(IP_READ), .out3(BX_READ), .out4(BY_READ), .out5(BZ_READ), .out6(ALU_READ),
    .sel(MICROINSTRUCTIONS_data[9:6]));  // open: out0, out7, out8, out9, out10, out11, out12, out13, out14, out15
  and and_1 (and_1_out, ADDR_q_2[15], ADDR_q_2[14], ADDR_q_2[13], ADDR_q_2[12]);
  DipSwitch #(.number(16)) dipswitch_1 (
    .sw1(dipswitch_1_sw16[15]), .sw2(dipswitch_1_sw16[14]), .sw3(dipswitch_1_sw16[13]),
    .sw4(dipswitch_1_sw16[12]), .sw5(dipswitch_1_sw16[11]), .sw6(dipswitch_1_sw16[10]),
    .sw7(dipswitch_1_sw16[9]), .sw8(dipswitch_1_sw16[8]), .sw9(dipswitch_1_sw16[7]),
    .sw10(dipswitch_1_sw16[6]), .sw11(dipswitch_1_sw16[5]), .sw12(dipswitch_1_sw16[4]),
    .sw13(dipswitch_1_sw16[3]), .sw14(dipswitch_1_sw16[2]), .sw15(dipswitch_1_sw16[1]),
    .sw16(dipswitch_1_sw16[0]));
  and and_2 (and_2_out, RAM_WRITE, not_2_out);
  not not_2 (not_2_out, and_1_out);
  and and_3 (and_3_out, and_1_out, demultiplexer_1_out2);
  and and_4 (and_4_out, and_1_out, demultiplexer_1_out3);
  and and_5 (and_5_out, and_1_out, demultiplexer_1_out4);
  and and_6 (and_6_out, and_1_out, demultiplexer_1_out5);
  and and_7 (and_7_out, and_1_out, demultiplexer_1_out0);
  and and_8 (and_8_out, and_1_out, demultiplexer_1_out1);
  Decoder #(.enable("false"), .select(4)) decoder_2 (
    .out1(RAM_WRITE), .out2(ADDR_WRITE), .out3(INST_WRITE), .out4(IP_WRITE), .out5(BX_WRITE),
    .out6(BY_WRITE), .out7(BZ_WRITE), .sel(MICROINSTRUCTIONS_data[13:10]));  // open: out0, out8, out9, out10, out11, out12, out13, out14, out15
  RAM #(.addrWidth(16), .asyncread("true"), .dataWidth(16), .\type ("nonvolatile")) ram_1 (
    .addr({ADDR_q_2, ADDR_q}), .we(and_2_out), .oe(1'b1), .clk(CLK), .din(DBUS), .dout(ram_1_dout));
  Multiplexer #(.width(16)) multiplexer_1 (.in0(ALU_IN_X), .in1({16{1'b0}}), .out(multiplexer_1_out), .sel(ALU_ZX));
  Multiplexer #(.width(16)) multiplexer_2 (.in0(ALU_IN_Y), .in1({16{1'b0}}), .out(multiplexer_2_out), .sel(ALU_ZY));
  Register #(.width(16)) register_1 (.D(DBUS), .en(and_9_out), .clk(CLK), .Q(register_1_q));  // open: clr
  and and_9 (and_9_out, RAM_WRITE, and_3_out);
  Register #(.width(16)) register_2 (.D(DBUS), .en(and_10_out), .clk(CLK), .Q(register_2_q));  // open: clr
  and and_10 (and_10_out, RAM_WRITE, and_4_out);
  Register #(.width(16)) register_3 (.D(DBUS), .en(and_11_out), .clk(CLK), .Q(register_3_q));  // open: clr
  and and_11 (and_11_out, RAM_WRITE, and_5_out);
  Register #(.width(16)) register_4 (.D(DBUS), .en(and_12_out), .clk(CLK), .Q(register_4_q));  // open: clr
  and and_12 (and_12_out, RAM_WRITE, and_6_out);
  Register #(.width(16)) register_5 (.D(DBUS), .en(and_13_out), .clk(CLK), .Q(register_5_q));  // open: clr
  and and_13 (and_13_out, RAM_WRITE, and_7_out);
  Register #(.width(16)) register_6 (.D(dipswitch_1_sw16), .en(1'b1), .clk(CLK), .Q(register_6_q));  // open: clr
  Multiplexer #(.width(16)) multiplexer_3 (
    .in0(multiplexer_1_out), .in1(not_3_out), .out(multiplexer_3_out), .sel(ALU_NX));
  assign not_3_out = ~multiplexer_1_out;  // NOT_Gate not_3, 16 bits wide
  Multiplexer #(.width(16)) multiplexer_4 (
    .in0(multiplexer_2_out), .in1(not_4_out), .out(multiplexer_4_out), .sel(ALU_NY));
  assign not_4_out = ~multiplexer_2_out;  // NOT_Gate not_4, 16 bits wide
  and and_14 (and_14_out, RAM_READ, not_2_out);
  assign and_15_out = multiplexer_3_out & multiplexer_4_out;  // AND_Gate and_15, 16 bits wide
  Adder #(.width(16)) adder_1 (
    .a(multiplexer_3_out), .b(multiplexer_4_out), .out(adder_1_out), .cin(1'b0));  // open: cout
  assign DBUS = and_14_out ? ram_1_dout : 16'bz;  // Controlled_Buffer controlled_buffer_5
  DotMatrix #(.matrixcols(8), .matrixrows(8)) dotmatrix_1 (
    .col0(register_1_q[7:0]), .col1(register_1_q[15:8]), .col2(register_2_q[7:0]), .col3(register_2_q[15:8]),
    .col4(register_3_q[7:0]), .col5(register_3_q[15:8]), .col6(register_4_q[7:0]), .col7(register_4_q[15:8]));
  Multiplexer #(.width(16)) multiplexer_5 (.in0(and_15_out), .in1(adder_1_out), .out(multiplexer_5_out), .sel(ALU_F));
  assign not_5_out = ~multiplexer_5_out;  // NOT_Gate not_5, 16 bits wide
  and and_16 (and_16_out, RAM_READ, and_8_out);
  assign DBUS = and_16_out ? register_6_q : 16'bz;  // Controlled_Buffer controlled_buffer_6
  Multiplexer #(.width(16)) multiplexer_6 (
    .in0(multiplexer_5_out), .in1(not_5_out), .out({ALU_OUT_NEG, multiplexer_6_out}), .sel(ALU_NO));
  assign DBUS = ALU_READ ? {ALU_OUT_NEG, multiplexer_6_out} : 16'bz;  // Controlled_Buffer controlled_buffer_7
  nor nor_1 (ALU_OUT_ZERO, multiplexer_6_out[0], multiplexer_6_out[1], multiplexer_6_out[2], multiplexer_6_out[3], multiplexer_6_out[4], multiplexer_6_out[5], multiplexer_6_out[6], multiplexer_6_out[7], multiplexer_6_out[8], multiplexer_6_out[9], multiplexer_6_out[10], multiplexer_6_out[11], multiplexer_6_out[12], multiplexer_6_out[13], multiplexer_6_out[14], ALU_OUT_NEG);
  Hex_Digit_Display hex_digit_display_1 (.value(register_5_q[15:12]));  // open: dp
  Hex_Digit_Display hex_digit_display_2 (.value(register_5_q[11:8]));  // open: dp
  Hex_Digit_Display hex_digit_display_3 (.value(register_5_q[7:4]));  // open: dp
  Hex_Digit_Display hex_digit_display_4 (.value(register_5_q[3:0]));  // open: dp

  // Notes on the sheet:
  //   contents of MICROINSTRUCTIONS (hex, n*v repeats v):
  //   2*880 2*4c40 2*8000 10*0 2*880 2*4c40 2*880 2*5040 2*8000 6*0 2*880 2*4c40 2*15be 2*8000 8*0 2*880
  //   2*4c40 2*159c 2*8000 8*0 2*880 2*4c40 2*880 2*5440 2*8000 6*0 2*880 2*4c40 2*880 2*4840 2*4c0 2*8000
  //   4*0 2*880 2*4c40 2*880 2*4840 2*1440 2*8000 4*0 2*880 2*4c40 2*88c 400c 504c 2*8000 6*0 2*880 2*4c40
  //   2*19bb 2*8000 8*0 2*880 2*4c40 2*1993 2*8000 8*0 2*880 2*4c40 2*880 2*5840 2*8000 6*0 2*880 2*4c40
  //   2*880 2*4840 2*500 2*8000 4*0 2*880 2*4c40 2*880 2*4840 2*1840 2*8000 4*0 2*880 2*4c40 2*883 4003
  //   5043 2*8000 6*0 2*880 2*4c40 2*18c0 2*8000 8*0 2*880 2*4c40 2*1500 2*8000 8*0 2*880 2*4c40 2*1cc0
  //   2*8000 8*0 2*880 2*4c40 2*1d00 2*8000 8*0 2*880 2*4c40 2*1540 2*8000 8*0 2*880 2*4c40 2*1940 2*8000
  //   8*0 2*880 2*4c40 2*1590 2*8000 8*0 2*880 2*4c40 2*1990 2*8000 8*0 2*880 2*4c40 2*15b2 2*8000 8*0
  //   2*880 2*4c40 2*19b8 2*8000 8*0 2*880 2*4c40 2*15b8 2*8000 8*0 2*880 2*4c40 2*15aa 2*8000
endmodule
