// Logisim project u16a.old.circ as structural Verilog: 2 circuits, main circuit main
module main (
);

  wire ADDR_X_WRITE_0, ADDR_X_WRITE_1, ADDR_Y_WRITE_0, ADDR_Y_WRITE_1, and_2_out, ARG_0_X_READ_0,
       ARG_0_X_READ_1, ARG_0_X_WRITE_0, ARG_0_X_WRITE_1, ARG_0_Y_READ_0, ARG_0_Y_READ_1, ARG_0_Y_WRITE_0,
       ARG_0_Y_WRITE_1, ARG_1_X_READ_0, ARG_1_X_READ_1, ARG_1_Y_READ_0, ARG_1_Y_READ_1, ARGS_WRITE_0,
       ARGS_WRITE_1, CLK, demultiplexer_2_out9, demultiplexer_2_out10, demultiplexer_2_out11,
       demultiplexer_2_out12, demultiplexer_2_out13, demultiplexer_2_out14, demultiplexer_2_out15,
       demultiplexer_4_out9, demultiplexer_4_out10, demultiplexer_4_out11, demultiplexer_4_out12,
       demultiplexer_4_out13, demultiplexer_4_out14, demultiplexer_4_out15, INST_STEP_RESET, INST_WIDTH,
       INST_WRITE_0, INST_WRITE_1, INV_CLK, IP_COUNT, IP_X_carry, IP_X_READ_0, IP_X_READ_1, IP_X_WRITE_0,
       IP_X_WRITE_1, IP_Y_READ_0, IP_Y_READ_1, IP_Y_WRITE_0, IP_Y_WRITE_1, or_1_out, or_2_out, or_3_out,
       or_4_out, or_5_out, or_6_out, or_7_out, RAM_READ_0, RAM_READ_1, xor_1_out, xor_2_out;
  wire [3:0] ARG_0, ARG_1, INST_STEP_q;
  wire [7:0] ADDR_X_q, ADDR_Y_q, BUS_0, BUS_1, controlled_buffer_1_out, controlled_buffer_7_out,
       controlled_buffer_9_out, controlled_buffer_13_out, controlled_buffer_15_out, controlled_buffer_17_out,
       controlled_buffer_21_out, INST_q, IP_X_q, IP_Y_q, ram_1_dout, undriven;
  wire [13:0] MICROINSTRUCTIONS_data;

  assign controlled_buffer_1_out = 1'b0 ? BUS_0 : 8'bz;  // Controlled_Buffer controlled_buffer_1
  or or_1 (or_1_out, 1'b0, 1'b0);
  assign controlled_buffer_1_out = 1'b0 ? BUS_1 : 8'bz;  // Controlled_Buffer controlled_buffer_2
  Counter IP_X (
    .clr(1'b0), .load(or_1_out), .up(1'b1), .count(IP_COUNT), .clk(CLK), .D(controlled_buffer_1_out),
    .carry(IP_X_carry), .Q(IP_X_q));
  assign BUS_0 = 1'b0 ? undriven : 8'bz;  // Controlled_Buffer controlled_buffer_3
  assign BUS_1 = 1'b0 ? undriven : 8'bz;  // Controlled_Buffer controlled_buffer_4
  assign BUS_0 = 1'b0 ? IP_X_q : 8'bz;  // Controlled_Buffer controlled_buffer_5
  assign BUS_1 = 1'b0 ? IP_X_q : 8'bz;  // Controlled_Buffer controlled_buffer_6
  assign controlled_buffer_7_out = 1'b0 ? BUS_0 : 8'bz;  // Controlled_Buffer controlled_buffer_7
  assign controlled_buffer_7_out = 1'b0 ? BUS_1 : 8'bz;  // Controlled_Buffer controlled_buffer_8
  assign controlled_buffer_9_out = 1'b0 ? BUS_0 : 8'bz;  // Controlled_Buffer controlled_buffer_9
  or or_2 (or_2_out, 1'b0, 1'b0);
  assign controlled_buffer_9_out = 1'b0 ? BUS_1 : 8'bz;  // Controlled_Buffer controlled_buffer_10
  or or_3 (or_3_out, 1'b0, 1'b0);
  Counter IP_Y (
    .clr(1'b0), .load(or_3_out), .up(IP_X_carry), .count(IP_X_carry), .clk(CLK), .D(controlled_buffer_7_out),
    .Q(IP_Y_q));  // open: carry
  assign BUS_0 = 1'b0 ? IP_Y_q : 8'bz;  // Controlled_Buffer controlled_buffer_11
  assign BUS_1 = 1'b0 ? IP_Y_q : 8'bz;  // Controlled_Buffer controlled_buffer_12
  Clock clock_1 (.out(CLK));
  not not_1 (INV_CLK, CLK);
  Counter #(.max('hf), .width(4)) INST_STEP (
    .clr(INST_STEP_RESET), .load(1'b0), .up(1'b1), .count(1'b1), .clk(INV_CLK), .D(4'b0000), .Q(INST_STEP_q));  // open: carry
  assign controlled_buffer_13_out = INST_WRITE_0 ? BUS_0 : 8'bz;  // Controlled_Buffer controlled_buffer_13
  assign controlled_buffer_13_out = INST_WRITE_1 ? BUS_1 : 8'bz;  // Controlled_Buffer controlled_buffer_14
  assign controlled_buffer_15_out = ADDR_X_WRITE_0 ? BUS_0 : 8'bz;  // Controlled_Buffer controlled_buffer_15
  assign controlled_buffer_15_out = ADDR_X_WRITE_1 ? BUS_1 : 8'bz;  // Controlled_Buffer controlled_buffer_16
  assign controlled_buffer_17_out = ADDR_Y_WRITE_0 ? BUS_0 : 8'bz;  // Controlled_Buffer controlled_buffer_17
  assign controlled_buffer_17_out = ADDR_Y_WRITE_1 ? BUS_1 : 8'bz;  // Controlled_Buffer controlled_buffer_18
  Register INST (.D(controlled_buffer_13_out), .en(or_4_out), .clk(CLK), .Q(INST_q));  // open: clr
  or or_4 (or_4_out, INST_WRITE_0, INST_WRITE_1);
  Register ADDR_X (.D(controlled_buffer_15_out), .en(or_5_out), .clk(CLK), .Q(ADDR_X_q));  // open: clr
  or or_5 (or_5_out, ADDR_X_WRITE_0, ADDR_X_WRITE_1);
  Register ADDR_Y (.D(controlled_buffer_17_out), .en(or_6_out), .clk(CLK), .Q(ADDR_Y_q));  // open: clr
  or or_6 (or_6_out, ADDR_Y_WRITE_0, ADDR_Y_WRITE_1);
  ROM #(.addrWidth(13), .dataWidth(16)) MICROINSTRUCTIONS (
    .addr({INST_q, INST_STEP_q, INST_WIDTH}), .data({INST_STEP_RESET, IP_COUNT, MICROINSTRUCTIONS_data}));
  RAM #(.addrWidth(16), .asyncread("true"), .\type ("nonvolatile")) ram_1 (
    .addr({ADDR_Y_q, ADDR_X_q}), .we(1'b0), .oe(1'b1), .clk(CLK), .dout(ram_1_dout));  // open: din
  // Probe on {INST_STEP_RESET, IP_COUNT, MICROINSTRUCTIONS_data}
  Demultiplexer #(.select(3)) demultiplexer_1 (
    .out1(ARG_0_X_READ_0), .out2(ARG_0_Y_READ_0), .out3(ARG_1_X_READ_0), .out4(ARG_1_Y_READ_0),
    .out5(IP_X_READ_0), .out6(IP_Y_READ_0), .out7(RAM_READ_0), .in(1'b1), .sel(MICROINSTRUCTIONS_data[2:0]));  // open: out0
  assign BUS_0 = RAM_READ_0 ? ram_1_dout : 8'bz;  // Controlled_Buffer controlled_buffer_19
  assign BUS_1 = RAM_READ_1 ? ram_1_dout : 8'bz;  // Controlled_Buffer controlled_buffer_20
  Demultiplexer #(.select(4)) demultiplexer_2 (
    .out1(ADDR_X_WRITE_0), .out2(ADDR_Y_WRITE_0), .out3(ARG_0_X_WRITE_0), .out4(ARG_0_Y_WRITE_0),
    .out5(IP_X_WRITE_0), .out6(IP_Y_WRITE_0), .out7(INST_WRITE_0), .out8(ARGS_WRITE_0),
    .out9(demultiplexer_2_out9), .out10(demultiplexer_2_out10), .out11(demultiplexer_2_out11),
    .out12(demultiplexer_2_out12), .out13(demultiplexer_2_out13), .out14(demultiplexer_2_out14),
    .out15(demultiplexer_2_out15), .in(1'b1), .sel(MICROINSTRUCTIONS_data[6:3]));  // open: out0
  Demultiplexer #(.select(3)) demultiplexer_3 (
    .out1(ARG_0_X_READ_1), .out2(ARG_0_Y_READ_1), .out3(ARG_1_X_READ_1), .out4(ARG_1_Y_READ_1),
    .out5(IP_X_READ_1), .out6(IP_Y_READ_1), .out7(RAM_READ_1), .in(1'b1), .sel(MICROINSTRUCTIONS_data[9:7]));  // open: out0
  Demultiplexer #(.select(4)) demultiplexer_4 (
    .out1(ADDR_X_WRITE_1), .out2(ADDR_Y_WRITE_1), .out3(ARG_0_X_WRITE_1), .out4(ARG_0_Y_WRITE_1),
    .out5(IP_X_WRITE_1), .out6(IP_Y_WRITE_1), .out7(INST_WRITE_1), .out8(ARGS_WRITE_1),
    .out9(demultiplexer_4_out9), .out10(demultiplexer_4_out10), .out11(demultiplexer_4_out11),
    .out12(demultiplexer_4_out12), .out13(demultiplexer_4_out13), .out14(demultiplexer_4_out14),
    .out15(demultiplexer_4_out15), .in(1'b1), .sel(MICROINSTRUCTIONS_data[13:10]));  // open: out0
  assign controlled_buffer_21_out = ARGS_WRITE_0 ? BUS_0 : 8'bz;  // Controlled_Buffer controlled_buffer_21
  or or_7 (or_7_out, ARGS_WRITE_0, ARGS_WRITE_1);
  assign controlled_buffer_21_out = ARGS_WRITE_1 ? BUS_1 : 8'bz;  // Controlled_Buffer controlled_buffer_22
  Register ARGS (.D(controlled_buffer_21_out), .en(or_7_out), .clk(CLK), .Q({ARG_1, ARG_0}));  // open: clr
  and and_1 (INST_WIDTH, ARG_0[2], ARG_0[3]);
  xor xor_1 (xor_1_out, ARG_0[2], ARG_0[3]);
  and and_2 (and_2_out, ARG_1[2], ARG_1[3]);
  xor xor_2 (xor_2_out, ARG_1[2], ARG_1[3]);

  // Notes on the sheet:
  //   Prefabs
  //   Instruction Parsing
  //   Is word
  //   Is byte
  //   Is word
  //   Is byte
endmodule

module ALU (
  input  zx,
  input  nx,
  input  f,
  input  no,
  input  [15:0] x,
  input  zy,
  input  nz,
  input  [15:0] y,
  output [15:0] o,
  output zr,
  output ng
);

  wire [15:0] adder_1_out, and_1_out, multiplexer_1_out, multiplexer_2_out, multiplexer_3_out,
       multiplexer_4_out, multiplexer_5_out, not_1_out, not_2_out, not_3_out;

  Multiplexer #(.width(16)) multiplexer_1 (.in0(x), .in1({16{1'b0}}), .out(multiplexer_1_out), .sel(zx));
  Multiplexer #(.width(16)) multiplexer_2 (.in0(y), .in1({16{1'b0}}), .out(multiplexer_2_out), .sel(zy));
  assign not_1_out = ~multiplexer_1_out;  // NOT_Gate not_1, 16 bits wide
  assign not_2_out = ~multiplexer_2_out;  // NOT_Gate not_2, 16 bits wide
  Multiplexer #(.width(16)) multiplexer_3 (.in0(multiplexer_1_out), .in1(not_1_out), .out(multiplexer_3_out), .sel(nx));
  Multiplexer #(.width(16)) multiplexer_4 (.in0(multiplexer_2_out), .in1(not_2_out), .out(multiplexer_4_out), .sel(nz));
  assign and_1_out = multiplexer_3_out & multiplexer_4_out;  // AND_Gate and_1, 16 bits wide
  Adder #(.width(16)) adder_1 (.a(multiplexer_3_out), .b(multiplexer_4_out), .out(adder_1_out));  // open: cin, cout
  and and_2 (zr, o[0], o[1], o[2], o[3], o[4], o[5], o[6], o[7], o[8], o[9], o[10], o[11], o[12], o[13], o[14], ng);
  Multiplexer #(.width(16)) multiplexer_5 (.in0(and_1_out), .in1(adder_1_out), .out(multiplexer_5_out), .sel(f));
  assign not_3_out = ~multiplexer_5_out;  // NOT_Gate not_3, 16 bits wide
  Multiplexer #(.width(16)) multiplexer_6 (.in0(multiplexer_5_out), .in1(not_3_out), .out({ng, o[14:0]}), .sel(no));

  assign o[15] = ng;
endmodule
